# Fritzing sketch Schema (saved by Fritzing 0.9.3b)
breadboards: 2

parts:
  S8 = Pushbutton [package="[THT]"]
  Part1 = Arduino Uno (Rev3)
  S9 = Pushbutton [package="[THT]"]
  S10 = Pushbutton [package="[THT]"]
  S11 = Pushbutton [package="[THT]"]
  R1 = Resistor [tolerance=±5% resistance=1k package=THT]
  DI1 = 7-Segment LED Display [package=THT]

nets:
  N1: S8.Pin_1, S8.Pin_2, Part1.D13/SCK
  N2: S8.Pin_3, S8.Pin_4, Part1.GND, S9.Pin_3, S9.Pin_4, S10.Pin_3, S10.Pin_4, S11.Pin_3, S11.Pin_4
  N3: Part1.D8, DI1.cathodeD
  N4: Part1.D9_PWM, DI1.cathodeE
  N5: Part1.D10_PWM/SS, S11.Pin_1, S11.Pin_2
  N6: Part1.D11_PWM/MOSI, S10.Pin_1, S10.Pin_2
  N7: Part1.D12/MISO, S9.Pin_1, S9.Pin_2
  N8: Part1.D2, DI1.cathodeDP
  N9: Part1.D3_PWM, DI1.cathodeC
  N10: Part1.D4, DI1.cathodeB
  N11: Part1.D5_PWM, DI1.cathodeA
  N12: Part1.D6_PWM, DI1.cathodeF
  N13: Part1.D7, DI1.cathodeG
  N14: Part1.5V, R1.Pin_1
  N15: R1.Pin_0, DI1.commAnode#7

notes:
  RED
  YELLOW
  GREEN
  BLUE
